# Fritzing sketch Diagrama Solar Tracker -  Arduino Nano (saved by Fritzing 1.0.0rc)
circuit board: 16.9333cm x 5.64444cm
breadboards: 1

parts:
  LED_ModoManual = LED - 5mm [color="Blue (505nm)" current=0.030A package="5 mm [THT]"]
  LED_SoloMotorHorizontal = LED - 5mm [color="Blue (505nm)" current=0.030A package="5 mm [THT]"]
  LED_ModoAutomatico = LED - 5mm [color="Blue (525nm)" current=0.030A part_number=Led_BTN_Automatico package="5 mm [THT]"]
  R6-LEDModoAutomatico = Resistor [tolerance=±5% resistance=220 power=0.25W package=THT]
  R2-Right_-_10k = Resistor [tolerance=±5% resistance=10k power=0.25W package=THT]
  R3_-_Down_10k = Resistor [tolerance=±5% resistance=10k power=0.25W package=THT]
  R4_-UP_10k = Resistor [tolerance=±5% resistance=10k power=0.25W package=THT]
  R1-_Left_10k = Resistor [tolerance=±5% resistance=10k power=0.25W package=THT]
  LDR_2_Right = Photocell (LDR) [power=0.25W dark_resistance_@0.01lx=300kΩ light_resistance_@100lx=400Ω luminance=10lx package=THT]
  LDR_3_UP_PIN_A3 = Photocell (LDR) [power=0.25W dark_resistance_@0.01lx=300kΩ light_resistance_@100lx=400Ω luminance=10lx package=THT]
  LDR_4_Down_PIN_A2 = Photocell (LDR) [power=0.25W dark_resistance_@0.01lx=300kΩ light_resistance_@100lx=400Ω luminance=10lx package=THT]
  Sensor_Amperaje_ACS712 = ACS712 Current Sensor 5A 20A 30A
  Joystick_KY_023 = Thumb Joystick
  BTN_ModoManual = Momentary Switch [package=ksa_sealed_tac_switch]
  Switch-_Encendido = Round Pushbutton
  BTN_ModoAutomatico = Momentary Switch [package=ksa_sealed_tac_switch]
  BTN_SoloMotorHorizontal = Momentary Switch [package=ksa_sealed_tac_switch]
  R8-BtnModoManual = Resistor [tolerance=±5% power=0.25W resistance=10 package=THT]
  R9-BtnModoSoloUnMotor = Resistor [tolerance=±5% power=0.25W resistance=10 package=THT]
  R10-ModoAutomatico = Resistor [tolerance=±5% power=0.25W resistance=10 package=THT]
  R6-LEDModoSoloUnMotor = Resistor [tolerance=±5% power=0.25W resistance=220 package=THT]
  R5-LED_ModoManual = Resistor [tolerance=±5% power=0.25W resistance=220 package=THT]
  Sensor_Voltaje = Voltage Sensor 25V
  LDR_1_Left = Photocell (LDR) [power=0.25W dark_resistance_@0.01lx=300kΩ light_resistance_@100lx=400Ω luminance=10lx package=THT]
  Foto_Celda = Solar Pannel [part_number=FotoSelda]
  Regulado_Voltaje_DC-DC_-12V_5V-5_7A = Mini-360 DC-DC Buck converter [package=THT]
  Mod2 = Solar Charge Controller [part_number="KLD Series Solar Charge Controller PWM" package=PWM-Model]
  Servo_Horizonal = Basic Servo [part_number="HiTec HS-422"]
  Componente1 = Arduino Nano (Rev3.0)
  Bat_1 = battery_holder_single_18650
  Bat_2 = battery_holder_single_18650
  Bat_3 = battery_holder_single_18650
  Bat5 = battery_holder_single_18650
  Mod1 = 3S-BMS
  Bat4 = battery_holder_single_18650
  Bat6 = battery_holder_single_18650
  Servo_Vertical = Basic Servo [part_number="HiTec HS-422"]

nets (from the schematic view):
  N1: LED_ModoManual.cathode, LED_SoloMotorHorizontal.cathode, LED_ModoAutomatico.cathode, Sensor_Amperaje_ACS712.GND
  N2: LED_ModoManual.anode, R5-LED_ModoManual.Pin_1
  N3: LED_SoloMotorHorizontal.anode, R6-LEDModoSoloUnMotor.Pin_1
  N4: LED_ModoAutomatico.anode, R6-LEDModoAutomatico.Pin_1
  N5: R6-LEDModoAutomatico.Pin_0, Componente1.D8
  N6: R2-Right_-_10k.Pin_0, LDR_2_Right.pin_1, Componente1.A1
  GND: R2-Right_-_10k.Pin_1, R3_-_Down_10k.Pin_0, R4_-UP_10k.Pin_0, Joystick_KY_023.GND, R8-BtnModoManual.Pin_0, R9-BtnModoSoloUnMotor.Pin_0, R10-ModoAutomatico.Pin_0, Sensor_Voltaje.GND, Regulado_Voltaje_DC-DC_-12V_5V-5_7A.OUT+, Servo_Horizonal.gnd, Componente1.GND, Componente1.D4, Servo_Vertical.gnd
  N7: R3_-_Down_10k.Pin_1, LDR_4_Down_PIN_A2.pin_1, Componente1.A2
  N8: R4_-UP_10k.Pin_1, LDR_3_UP_PIN_A3.pin_1, Componente1.A0
  N9: R1-_Left_10k.Pin_0, LDR_1_Left.pin_1, Componente1.A3
  VCC: LDR_2_Right.pin_0, LDR_3_UP_PIN_A3.pin_0, LDR_4_Down_PIN_A2.pin_0, Sensor_Amperaje_ACS712.2, Sensor_Amperaje_ACS712.VCC, Sensor_Amperaje_ACS712.OUT, Joystick_KY_023.VCC, BTN_ModoManual.2, Switch-_Encendido.leg1, BTN_ModoAutomatico.2, BTN_SoloMotorHorizontal.2, Sensor_Voltaje.VCC, Sensor_Voltaje.+, LDR_1_Left.pin_0, Regulado_Voltaje_DC-DC_-12V_5V-5_7A.IN+, Mod2.Connector_5, Servo_Horizonal.vcc, Componente1.VIN, Componente1.A6, Servo_Vertical.vcc
  N10: Sensor_Amperaje_ACS712.1, Foto_Celda.pin2
  N11: Joystick_KY_023.HORZ, Componente1.A4
  N12: Joystick_KY_023.VERT, Componente1.A5
  N13: BTN_ModoManual.4, R8-BtnModoManual.Pin_1, Componente1.D2
  N14: Switch-_Encendido.leg0, Regulado_Voltaje_DC-DC_-12V_5V-5_7A.OUT-
  N15: BTN_ModoAutomatico.4, R10-ModoAutomatico.Pin_1
  N16: BTN_SoloMotorHorizontal.4, R9-BtnModoSoloUnMotor.Pin_1, Componente1.D3
  N17: R6-LEDModoSoloUnMotor.Pin_0, Componente1.D9
  N18: R5-LED_ModoManual.Pin_0, Componente1.D7
  N19: Sensor_Voltaje.S, Componente1.A7
  N20: Sensor_Voltaje.-, Foto_Celda.pin1, Regulado_Voltaje_DC-DC_-12V_5V-5_7A.IN-, Mod2.Connector_6
  N21: Mod2.Connector_3, Mod1.+
  N22: Mod2.Connector_4, Mod1.-
  N23: Servo_Horizonal.pulse, Componente1.D11/MOSI
  N24: Componente1.D10, Servo_Vertical.pulse
  N25: Bat_1.+#0, Bat_2.+#0, Mod1.12.6V
  N26: Bat_1.+#1, Bat_2.+#1, Bat_3.+#0, Mod1.8.4V, Bat4.+#0
  N27: Bat_3.+#1, Bat5.+#0, Mod1.4.2V, Bat4.+#1, Bat6.+#0
  N28: Bat5.+#1, Mod1.0V, Bat6.+#1

custom parts:
  ACS712 Current Sensor 5A 20A 30A: Remix by Michael Kubina http://www.kubina.info Original by: https://forum.fritzing.org/t/current-sensor-5a-acs712/7694 https://forum.fritzing.org/u/ArtHome ArtHome12@gmail.com
  Mini-360 DC-DC Buck converter: Mini-360 DC-DC Buck converter. Tiny buck step down voltage converter, input voltage 4.75 to 23V output 1 to 17V adjustable. Available from ebay and the like.
  Solar Charge Controller: PWM-Solar Charge Controller
  battery_holder_single_18650: single 18650 battery holder
  3S-BMS: 3S-BMS LIPO battery charger / protection unit. Note pcb does not match the board as it will likely connect with wires, so pcb is 6 pads suitable for .1in header pins.
