# Fritzing sketch Diagrama Solar Tracker (saved by Fritzing 1.0.0rc)
circuit board: 16.9333cm x 5.64444cm
breadboards: 1

parts:
  LED_ModoManual = LED - 5mm [color="Blue (505nm)" current=0.030A package="5 mm [THT]"]
  LED_SoloMotorHorizontal = LED - 5mm [color="Blue (505nm)" current=0.030A package="5 mm [THT]"]
  LED_ModoAutomatico = LED - 5mm [color="Blue (525nm)" current=0.030A part_number=Led_BTN_Automatico package="5 mm [THT]"]
  R6-LEDModoAutomatico = Resistor [tolerance=±5% resistance=220 power=0.25W package=THT]
  R2-Right_-_10k = Resistor [tolerance=±5% resistance=10k power=0.25W package=THT]
  R3_-_Down_10k = Resistor [tolerance=±5% resistance=10k power=0.25W package=THT]
  R4_-UP_10k = Resistor [tolerance=±5% resistance=10k power=0.25W package=THT]
  R1-_Left_10k = Resistor [tolerance=±5% resistance=10k power=0.25W package=THT]
  LDR_2_Right = Photocell (LDR) [power=0.25W dark_resistance_@0.01lx=300kΩ light_resistance_@100lx=400Ω luminance=10lx package=THT]
  LDR_3_UP_PIN_A3 = Photocell (LDR) [power=0.25W dark_resistance_@0.01lx=300kΩ light_resistance_@100lx=400Ω luminance=10lx package=THT]
  LDR_4_Down_PIN_A2 = Photocell (LDR) [power=0.25W dark_resistance_@0.01lx=300kΩ light_resistance_@100lx=400Ω luminance=10lx package=THT]
  Reloj_Tinyu_RTC = Tiny RTC
  Sensor_Amperaje_ACS712 = ACS712 Current Sensor 5A 20A 30A
  Pla_Cprincipal = Arduino Mega 2560 (Rev3)
  Pantalla_OLED_I2C1 = OLED 128x64 I2C Monochrome Display
  R12-MedirNivelBateria = Resistor [tolerance=±5% resistance=10k power=0.25W package=THT]
  Bluetooth = Bluetooth HC-06u [package=THT]
  Joystick_KY_023 = Thumb Joystick
  BTN_ModoManual = Momentary Switch [package=ksa_sealed_tac_switch]
  Switch-_Encendido = Round Pushbutton
  BTN_ModoAutomatico = Momentary Switch [package=ksa_sealed_tac_switch]
  BTN_SoloMotorHorizontal = Momentary Switch [package=ksa_sealed_tac_switch]
  R8-BtnModoManual = Resistor [tolerance=±5% power=0.25W resistance=10 package=THT]
  R9-BtnModoSoloUnMotor = Resistor [tolerance=±5% power=0.25W resistance=10 package=THT]
  R10-ModoAutomatico = Resistor [tolerance=±5% power=0.25W resistance=10 package=THT]
  R6-LEDModoSoloUnMotor = Resistor [tolerance=±5% power=0.25W resistance=220 package=THT]
  R5-LED_ModoManual = Resistor [tolerance=±5% power=0.25W resistance=220 package=THT]
  R18 = Resistor [tolerance=±5% power=0.25W resistance=220 package=THT]  # not connected
  LED_Encendido = LED - 5mm [color="Red (633nm)" current=0.030A package="5 mm [THT]"]  # not connected
  LED_Error = LED - 5mm [color="Red (633nm)" current=0.030A package="5 mm [THT]"]
  Sensor_Voltaje = Voltage Sensor 25V
  LDR_1_Left = Photocell (LDR) [power=0.25W dark_resistance_@0.01lx=300kΩ light_resistance_@100lx=400Ω luminance=10lx package=THT]
  R11-Led_ErrorSD = Resistor [tolerance=±5% power=0.25W resistance=220 package=THT]
  Bat_1 = battery_holder_single_18650
  Mod1 = 3S-BMS
  Bat6 = battery_holder_single_18650
  Bat5 = battery_holder_single_18650
  Bat4 = battery_holder_single_18650
  Foto_Celda = Solar Pannel [part_number=FotoSelda]
  Bat_3 = battery_holder_single_18650
  Bat_2 = battery_holder_single_18650
  Convertidor-Placa_Principal = Mini-360 DC-DC Buck converter [package=THT]
  Convertidor-Servo_Motores = Mini-360 DC-DC Buck converter [package=THT]
  Servo_Horizonal = Basic Servo [part_number="HiTec HS-422"]
  Servo_Vertical = Basic Servo [part_number="HiTec HS-422"]
  USB_Carga_Externa = USB Connectors [package=usb-a-s-silk-female]  # not connected
  SD_GuardarInfo = Full Size SD Card Module
  Mod2 = Solar Charge Controller [part_number="KLD Series Solar Charge Controller PWM" package=PWM-Model]

nets (from the schematic view):
  N1: LED_ModoManual.cathode, LED_SoloMotorHorizontal.cathode, LED_ModoAutomatico.cathode, Sensor_Amperaje_ACS712.GND
  N2: LED_ModoManual.anode, R5-LED_ModoManual.Pin_1
  N3: LED_SoloMotorHorizontal.anode, R6-LEDModoSoloUnMotor.Pin_1
  N4: LED_ModoAutomatico.anode, R6-LEDModoAutomatico.Pin_1
  N5: R6-LEDModoAutomatico.Pin_0, Pla_Cprincipal.D10_PWM
  N6: R2-Right_-_10k.Pin_0, LDR_2_Right.pin_1
  GND: R2-Right_-_10k.Pin_1, R3_-_Down_10k.Pin_0, R4_-UP_10k.Pin_0, R1-_Left_10k.Pin_1, Reloj_Tinyu_RTC.GND#10, Pla_Cprincipal.GND, Pantalla_OLED_I2C1.GND, Bluetooth.GND, Joystick_KY_023.GND, R8-BtnModoManual.Pin_0, R9-BtnModoSoloUnMotor.Pin_0, R10-ModoAutomatico.Pin_0, Sensor_Voltaje.-, Convertidor-Placa_Principal.OUT-, Convertidor-Servo_Motores.OUT-, Servo_Horizonal.gnd, Servo_Vertical.gnd, SD_GuardarInfo.pin_1, SD_GuardarInfo.pin_15
  N7: R3_-_Down_10k.Pin_1, LDR_4_Down_PIN_A2.pin_1
  N8: R4_-UP_10k.Pin_1, LDR_3_UP_PIN_A3.pin_1
  N9: R1-_Left_10k.Pin_0, LDR_1_Left.pin_1
  N10: LDR_2_Right.pin_0, Pla_Cprincipal.A1
  N11: LDR_3_UP_PIN_A3.pin_0, Pla_Cprincipal.A2
  N12: LDR_4_Down_PIN_A2.pin_0, Pla_Cprincipal.A3
  N13: Reloj_Tinyu_RTC.GND#4, LED_Error.cathode
  N14: Reloj_Tinyu_RTC.SCL, Pla_Cprincipal.D21/SCL, Pantalla_OLED_I2C1.SCK
  N15: Reloj_Tinyu_RTC.SDA, Pla_Cprincipal.D20/SDA, Pantalla_OLED_I2C1.SDA
  VCC: Reloj_Tinyu_RTC.VCC, Sensor_Amperaje_ACS712.VCC, Pla_Cprincipal.5V, Pantalla_OLED_I2C1.VDD, Bluetooth.VCC, Joystick_KY_023.VCC, BTN_ModoManual.2, BTN_ModoAutomatico.1, BTN_SoloMotorHorizontal.2, SD_GuardarInfo.pin_5, SD_GuardarInfo.pin_6
  N16: Sensor_Amperaje_ACS712.1, Mod2.Connector_1
  3V3: Sensor_Amperaje_ACS712.2, Sensor_Amperaje_ACS712.OUT, Pla_Cprincipal.A4, Pla_Cprincipal.3V3, Sensor_Voltaje.VCC, Sensor_Voltaje.+, Foto_Celda.pin1
  N17: Pla_Cprincipal.A8, Sensor_Voltaje.S
  N18: Pla_Cprincipal.A0, LDR_1_Left.pin_0
  N19: Pla_Cprincipal.A5, R12-MedirNivelBateria.Pin_1
  N20: Pla_Cprincipal.A6, Joystick_KY_023.HORZ
  N21: Pla_Cprincipal.A7, Joystick_KY_023.VERT
  N22: Pla_Cprincipal.D17_PWM/RX2, Bluetooth.TXD
  N23: Pla_Cprincipal.D16_PWM/TX2, Bluetooth.RXD
  N24: Pla_Cprincipal.D13_PWM, R11-Led_ErrorSD.Pin_1
  N25: Pla_Cprincipal.D12_PWM, R5-LED_ModoManual.Pin_0
  N26: Pla_Cprincipal.D11_PWM, R6-LEDModoSoloUnMotor.Pin_0
  N27: Pla_Cprincipal.VIN, Convertidor-Placa_Principal.OUT+
  N28: Pla_Cprincipal.D2_PWM, BTN_ModoAutomatico.4, R10-ModoAutomatico.Pin_1
  N29: Pla_Cprincipal.D3_PWM, BTN_SoloMotorHorizontal.4, R9-BtnModoSoloUnMotor.Pin_1
  N30: Pla_Cprincipal.D4_PWM, BTN_ModoManual.4, R8-BtnModoManual.Pin_1
  N31: Pla_Cprincipal.D6_PWM, Servo_Vertical.pulse
  N32: Pla_Cprincipal.D7_PWM, Servo_Horizonal.pulse
  N33: Pla_Cprincipal.D50, SD_GuardarInfo.pin_13
  N34: Pla_Cprincipal.D51, SD_GuardarInfo.pin_9
  N35: Pla_Cprincipal.D52, SD_GuardarInfo.pin_11
  N36: Pla_Cprincipal.D53, SD_GuardarInfo.pin_7
  N37: Switch-_Encendido.leg0, Mod2.Connector_5
  N38: Switch-_Encendido.leg1, Convertidor-Placa_Principal.IN+, Convertidor-Servo_Motores.IN+
  N39: LED_Error.anode, R11-Led_ErrorSD.Pin_0
  N40: Sensor_Voltaje.GND, Foto_Celda.pin2, Mod2.Connector_2
  N41: Bat_1.+#0, Mod1.12.6V, Bat_2.+#0
  N42: Bat_1.+#1, Mod1.8.4V, Bat4.+#0, Bat_3.+#0, Bat_2.+#1
  N43: Mod1.0V, Bat6.+#1, Bat5.+#1
  N44: Mod1.4.2V, Bat6.+#0, Bat5.+#0, Bat4.+#1, Bat_3.+#1
  N45: Mod1.-, Mod2.Connector_4
  N46: Mod1.+, Mod2.Connector_3
  N47: Convertidor-Placa_Principal.IN-, Convertidor-Servo_Motores.IN-, Mod2.Connector_6
  VCC_2: Convertidor-Servo_Motores.OUT+, Servo_Horizonal.vcc, Servo_Vertical.vcc

custom parts:
  Tiny RTC: Tiny RTC I2C module DS1370Z RTC and AT24C32 EEPROM
  ACS712 Current Sensor 5A 20A 30A: Remix by Michael Kubina http://www.kubina.info Original by: https://forum.fritzing.org/t/current-sensor-5a-acs712/7694 https://forum.fritzing.org/u/ArtHome ArtHome12@gmail.com
  Bluetooth HC-06u: Bluetooth HC-06 - face up, pins down 16.5mm x 37.5mm PCB
  battery_holder_single_18650: single 18650 battery holder
  3S-BMS: 3S-BMS LIPO battery charger / protection unit. Note pcb does not match the board as it will likely connect with wires, so pcb is 6 pads suitable for .1in header pins.
  Mini-360 DC-DC Buck converter: Mini-360 DC-DC Buck converter. Tiny buck step down voltage converter, input voltage 4.75 to 23V output 1 to 17V adjustable. Available from ebay and the like.
  Full Size SD Card Module: SD Card Module Slot Socket Reader For Arduino ARM MCU
  Solar Charge Controller: PWM-Solar Charge Controller
